// Logisim project test.circ as structural Verilog: 1 circuit, main circuit main
module main (
);

  wire and_1_out, and_2_out, and_3_out, and_4_out, and_5_out, and_6_out, clock_1_out, clock_2_out,
       clock_3_out, comparator_1_eq, comparator_2_eq, comparator_3_eq, comparator_4_eq, hard_drive_dma_1_p9,
       hard_drive_dma_1_p10, rv32im_cpu_1_p2, rv32im_cpu_1_p5, rv32im_cpu_1_p6, rv32im_cpu_1_p7,
       rv32im_cpu_1_p8, rv32im_cpu_1_p9, rv32im_cpu_1_p10, rv32im_cpu_1_p11;
  wire [31:0] rom_1_data, rv32im_cpu_1_p3, rv32im_cpu_1_p4;

  Clock clock_1 (.out(clock_1_out));
  // RV32IM_CPU #(.hexRegisters("true")) rv32im_cpu_1: pin names not known; wires that end beside it: clock_1_out, rv32im_cpu_1_p2, rv32im_cpu_1_p3, rv32im_cpu_1_p4, rv32im_cpu_1_p5, rv32im_cpu_1_p6, rv32im_cpu_1_p7, rv32im_cpu_1_p8, rv32im_cpu_1_p9, rv32im_cpu_1_p10, rv32im_cpu_1_p11
  Pull_Resistor pull_resistor_1 (.node(rv32im_cpu_1_p5));
  Pull_Resistor pull_resistor_2 (.node(rv32im_cpu_1_p6));
  and and_1 (and_1_out, rv32im_cpu_1_p6, comparator_4_eq);
  and and_2 (and_2_out, comparator_4_eq, rv32im_cpu_1_p5);
  Clock clock_2 (.out(clock_2_out));
  RAM #(.addrWidth(14), .asyncread("true"), .byteenables("byteEnables"), .dataWidth(32), .databus("bidir")) ram_1 (
    .addr(rv32im_cpu_1_p3[15:2]), .we(and_1_out), .oe(and_2_out), .clk(clock_2_out), .data(rv32im_cpu_1_p4),
    .be3(rv32im_cpu_1_p11), .be2(rv32im_cpu_1_p10), .be1(rv32im_cpu_1_p9), .be0(rv32im_cpu_1_p8));
  Comparator #(.width(32)) comparator_1 (.a(rv32im_cpu_1_p3), .b(32'hfff00000), .eq(comparator_1_eq));  // open: gt, lt
  Comparator #(.width(16)) comparator_2 (
    .a(rv32im_cpu_1_p3[31:16]), .b({16{1'b0}}), .eq(comparator_2_eq));  // open: gt, lt
  Comparator #(.width(16)) comparator_3 (.a(rv32im_cpu_1_p3[31:16]), .b(16'h11), .eq(comparator_3_eq));  // open: gt, lt
  Comparator #(.width(16)) comparator_4 (.a(rv32im_cpu_1_p3[31:16]), .b(16'h1), .eq(comparator_4_eq));  // open: gt, lt
  and and_3 (and_3_out, rv32im_cpu_1_p5, comparator_2_eq);
  ROM #(.addrWidth(11), .dataWidth(32)) rom_1 (.addr(rv32im_cpu_1_p3[12:2]), .data(rom_1_data));
  and and_4 (and_4_out, rv32im_cpu_1_p6, comparator_1_eq);
  Clock clock_3 (.out(clock_3_out));
  TTY tty_1 (.data(rv32im_cpu_1_p4[6:0]), .clk(clock_3_out), .we(and_4_out));  // open: clr
  assign rv32im_cpu_1_p4 = and_3_out ? rom_1_data : 32'bz;  // Controlled_Buffer controlled_buffer_1
  and and_5 (and_5_out, rv32im_cpu_1_p5, comparator_3_eq);
  and and_6 (and_6_out, rv32im_cpu_1_p6, comparator_3_eq);
  // Hard_Drive_DMA hard_drive_dma_1: pin names not known; wires that end beside it: rv32im_cpu_1_p3, and_5_out, and_6_out, rv32im_cpu_1_p11, rv32im_cpu_1_p10, rv32im_cpu_1_p9, rv32im_cpu_1_p8, rv32im_cpu_1_p7, hard_drive_dma_1_p9, hard_drive_dma_1_p10, hard_drive_dma_1_p10, rv32im_cpu_1_p4, rv32im_cpu_1_p5, rv32im_cpu_1_p6, rv32im_cpu_1_p3, rv32im_cpu_1_p2
  Clock clock_4 (.out(hard_drive_dma_1_p9));

  // Notes on the sheet:
  //   contents of rom_1 (hex, n*v repeats v):
  //   20117 ffc10113 513 593 613 38000ef 6f fe010113 812e23 2010413 50793 fef407a3 fff007b7 fef44703
  //   e78023 13 1c12403 2010113 8067 f5010113 a112623 a812423 b010413 2b00513 fbdff0ef 514000ef 50793
  //   7da63 4600513 fa9ff0ef fff00793 1900006f 464000ef 50793 7da63 4900513 f8dff0ef fff00793 1740006f
  //   100513 6a8000ef 50793 7da63 4f00513 f6dff0ef fff00793 1540006f 100513 2d8000ef fea42423 fe842783
  //   7da63 4500513 f49ff0ef fff00793 1300006f 107b7 78693 fe842703 70793 179793 e787b3 279793 f687b3
  //   300713 e7a423 17b7 24478793 fef42223 fe442503 6ed000ef 50793 78613 fe442583 fe842503 259000ef
  //   fea42023 fe442503 6cd000ef 50713 fe042783 f70a63 5700513 ed1ff0ef fff00793 b80006f 2d00513 ec1ff0ef
  //   593 fe842503 314000ef f4042e23 f6040793 7c00713 70613 593 78513 745000ef f5c40793 8000613 78593
  //   fe842503 688000ef fca42e23 fdc42783 7da63 5200513 e71ff0ef fff00793 580006f fdc42783 79a63 5a00513
  //   e59ff0ef 793 400006f fe042623 280006f fec42783 ff040713 f707b3 f6c7c783 78513 e31ff0ef fec42783
  //   178793 fef42623 fec42703 fdc42783 fcf74ae3 793 78513 ac12083 a812403 b010113 8067 ff010113 812623
  //   1010413 13 17b7 2587a783 7a783 17f793 fe0798e3 13 13 c12403 1010113 8067 fe010113 112e23 812c23
  //   2010413 fea42623 feb42423 fec42783 7cc63 107b7 c078793 47a783 fec42703 f74663 fff00793 580006f 17b7
  //   2507a783 fe842703 e7a023 17b7 2547a783 fec42703 e7a023 17b7 24c7a783 100713 e7a023 f5dff0ef 17b7
  //   2587a783 7a783 27f793 78663 fff00793 80006f 793 78513 1c12083 1812403 2010113 8067 fe010113 112e23
  //   812c23 2010413 fea42623 feb42423 107b7 c078793 47a783 fec42703 f74663 fff00793 580006f 17b7 2507a783
  //   fe842703 e7a023 17b7 2547a783 fec42703 e7a023 17b7 24c7a783 200713 e7a023 ec1ff0ef 17b7 2587a783
  //   7a783 27f793 78663 fff00793 80006f 793 78513 1c12083 1812403 2010113 8067 fd010113 2112623 2812423
  //   3010413 fca42e23 fdc42503 398000ef 50793 7d663 fff00793 a80006f 107b7 6d47a783 178693 10737 6cd72a23
  //   fef42623 fec42703 f00793 e7d663 fff00793 7c0006f 107b7 78693 fec42703 70793 179793 e787b3 279793
  //   f687b3 fdc42703 e7a223 107b7 78693 fec42703 70793 179793 e787b3 279793 f687b3 100713 e7a423 107b7
  //   78693 fec42703 70793 179793 e787b3 279793 f687b3 7a023 fec42783 78513 2c12083 2812403 3010113 8067
  //   fe010113 812e23 2010413 fea42623 feb42423 fec42783 407c063 fec42703 f00793 2e7ca63 fe842783 207c663
  //   107b7 78693 fec42703 70793 179793 e787b3 279793 f687b3 fe842703 e7a023 13 1c12403 2010113 8067
  //   ff010113 112623 812423 1010413 107b7 6c07aa23 107b7 c078593 100513 d51ff0ef 50793 7d663 fff00793
  //   4c0006f 107b7 c078793 7a783 79663 fff00793 340006f 107b7 c078793 87a703 107b7 d478593 70513 d0dff0ef
  //   50793 7d663 fff00793 80006f 793 78513 c12083 812403 1010113 8067 de010113 20112e23 20812c23 22010413
  //   107b7 6c07aa23 107b7 c078793 1000713 e7a023 107b7 c078793 40000713 e7a223 107b7 c078793 200713
  //   e7a423 107b7 c078793 300713 e7a623 107b7 c078793 500713 e7a823 107b7 c078593 100513 d11ff0ef 50793
  //   7d663 fff00793 1380006f fe042623 8c0006f fec42783 41f7d713 777713 f707b3 4037d793 78693 107b7
  //   d478793 d787b3 7c783 1879613 41865613 fec42703 41f75793 1d7d793 f70733 777713 40f707b3 78713 100793
  //   e797b3 1879793 4187d793 f667b3 1879793 4187d793 ff7f713 107b7 d478793 d787b3 e78023 fec42783 178793
  //   fef42623 107b7 c078793 107a783 fec42703 f6f744e3 107b7 c078793 87a703 107b7 d478593 70513 c41ff0ef
  //   50793 7d663 fff00793 680006f de042423 dec40793 1fc00713 70613 593 78513 1e1000ef 107b7 c078793
  //   c7a783 fef42423 200006f de840793 78593 fe842503 bf1ff0ef fe842783 178793 fef42423 107b7 c078793
  //   107a783 fe842703 fcf74ae3 793 78513 21c12083 21812403 22010113 8067 dd010113 22112623 22812423
  //   23010413 dca42e23 ddc42783 7cc63 107b7 c078793 7a783 ddc42703 f74663 fff00793 900006f 107b7 c078793
  //   c7a703 ddc42783 41f7d693 76f693 f687b3 4037d793 f707b3 fef42623 ddc42783 679713 41f75793 177d793
  //   f70733 1ff77713 40f707b3 fef42423 de840793 78593 fec42503 a85ff0ef ddc42783 679713 107b7 2d478793
  //   f706b3 fe842783 de840713 f707b3 4000613 78593 68513 125000ef ddc42783 78513 22c12083 22812403
  //   23010113 8067 dc010113 22112e23 22812c23 24010413 dca42623 dcb42423 dcc42223 dcc42783 407c063 10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
endmodule
